// Logisim project tal8643.circ as structural Verilog: 1 circuit, main circuit main
module main (
  input  p,
  input  q,
  input  r,
  input  s
);

  wire and_1_out, and_2_out, and_3_out, and_4_out, and_5_out, and_6_out, and_7_out, and_8_out, and_9_out,
       not_1_out, not_2_out, not_3_out, or_1_out, or_2_out, or_3_out, or_4_out, or_5_out, or_6_out, or_7_out;

  not not_1 (not_1_out, p);
  not not_2 (not_2_out, q);
  not not_3 (not_3_out, r);
  // NOT_Gate not_4 has open pins: in=s, out=open
  and and_1 (and_1_out, not_1_out, not_3_out);
  and and_2 (and_2_out, not_3_out, q);
  and and_3 (and_3_out, q, not_1_out);
  and and_4 (and_4_out, r, not_1_out, p);
  and and_5 (and_5_out, not_2_out, not_1_out);
  and and_6 (and_6_out, q, p);
  and and_7 (and_7_out, not_2_out, r);
  and and_8 (and_8_out, r, not_1_out);
  and and_9 (and_9_out, r, p);
  or or_1 (or_1_out, p, not_2_out, r);
  or or_2 (or_2_out, s, and_1_out, and_2_out, and_3_out, and_4_out);
  _7_Segment_Display u_7_segment_display_1 (
    .g(or_5_out), .f(or_6_out), .a(or_7_out), .b(or_4_out), .e(or_3_out), .d(or_2_out), .c(or_1_out),
    .dp(or_7_out));
  or or_3 (or_3_out, and_1_out, and_3_out);
  or or_4 (or_4_out, and_6_out, and_5_out, not_3_out);
  or or_5 (or_5_out, and_2_out, and_3_out, and_7_out, s);
  or or_6 (or_6_out, and_5_out, and_7_out, and_8_out, s);
  or or_7 (or_7_out, and_1_out, and_9_out, s, q);
endmodule
